# Fritzing sketch chanber_controller Sketch_m2 (saved by Fritzing 0.9.9b)
perfboards: 1

parts:
  Grove1 = Grove OLED 128x96  # not connected
  DHT1 = DHT22 Humidity and Temperature Sensor  # not connected
  Fan = LED - 5mm [color="Red (633nm)" current=0.030 package="5 mm [THT]"]
  Vents = LED - 5mm [color="Red (633nm)" current=0.030 package="5 mm [THT]"]
  Lights = LED - 5mm [color="Red (633nm)" current=0.030 package="5 mm [THT]"]
  U1 = atmega328 [package=dip]
  PB_Lights = Pushbutton [package="[SMD]"]
  R4 = Resistor [tolerance=±5% resistance=1k package="0805 [SMD]"]
  R5 = Resistor [tolerance=±5% resistance=1k package="0805 [SMD]"]
  R6 = Resistor [tolerance=±5% resistance=1k package="0805 [SMD]"]
  J1 = male pin header, 3 pins [form="♂ (male)"]
  PB_Fans = Pushbutton [package="[SMD]"]
  PB_Vents = Pushbutton [package="[SMD]"]
  J2 = Screw terminal - 2 pins [package=THT]
  C1 = Electrolytic Capacitor [capacitance=1µF voltage=35V package="100 mil [THT, electrolytic]"]
  C2 = Electrolytic Capacitor [capacitance=1µF voltage=35V package="100 mil [THT, electrolytic]"]
  U2 = Voltage Regulator - 5V [package="TO220 [THT]"]
  J3 = molex pin header, 1 pin [form=molex]
  VCC1 = Battery block 9V
  R7 = Resistor [tolerance=±5% resistance=220 package="0805 [SMD]"]
  R8 = Resistor [tolerance=±5% resistance=220 package="0805 [SMD]"]
  R9 = Resistor [tolerance=±5% resistance=220 package="0805 [SMD]"]
  J4 = male pin header, 2 pins [form="♂ (male)"]
  J5 = male pin header, 2 pins [form="♂ (male)"]
  J6 = male pin header, 2 pins [form="♂ (male)"]
  J7 = male pin header, 4 pins [form="♂ (male)"]  # not connected

nets:
  N1: Fan.cathode, U1.D6_(PWM), J6.pin2
  N2: Fan.anode, R9.Pin_0, J6.pin1
  N3: Vents.cathode, U1.D7, J5.pin2
  N4: Vents.anode, R8.Pin_0, J5.pin1
  N5: Lights.cathode, U1.D8, J4.pin2
  N6: Lights.anode, R7.Pin_0, J4.pin1
  N7: U1.D2, PB_Lights.Pin_1, PB_Lights.Pin_2, R4.Pin_1, J1.pin1
  N8: U1.D3_(PWM), R5.Pin_1, J1.pin2, PB_Vents.Pin_1, PB_Vents.Pin_2
  N9: U1.D4, R6.Pin_1, J1.pin3, PB_Fans.Pin_1, PB_Fans.Pin_2
  N10: U1.VCC, PB_Lights.Pin_3, PB_Lights.Pin_4, PB_Fans.Pin_3, PB_Fans.Pin_4, PB_Vents.Pin_3, PB_Vents.Pin_4, C2.+, U2.output_voltage, J3.pin1
  GND: U1.GND, R4.Pin_0, R5.Pin_0, R6.Pin_0, J2.pin2, C1.-, C2.-, U2.GND, VCC1.-, R7.Pin_1, R8.Pin_1, R9.Pin_1
  N11: J2.pin1, C1.+, U2.input_voltage, VCC1.+
